# Fritzing sketch led wiring (saved by Fritzing 0.9.10b)

parts:
  LED2 = smd LED [color="White (4500K)" package="0805 [SMD]"]
  Sign_Left = LED - 3mm [color="Yellow (595nm)" current=0.030 package="3 mm [THT]"]
  Head_Light = smd LED [color="White (4500K)" package="0805 [SMD]"]
  Sign_Right = LED - 3mm [color="Yellow (595nm)" current=0.030 package="3 mm [THT]"]
  LED5 = LED - 3mm [color="Yellow (595nm)" current=0.030 package="3 mm [THT]"]
  LED6 = LED - 3mm [color="Yellow (595nm)" current=0.030 package="3 mm [THT]"]
  LED7 = LED - 3mm [color="Red (660nm)" current=0.030 package="3 mm [THT]"]
  brake_light = LED - 3mm [color="Red (660nm)" current=0.030 package="3 mm [THT]"]
  LED9 = LED - 3mm [color="White (4500K)" current=0.030 package="3 mm [THT]"]
  Reverse_Light = LED - 3mm [color="White (4500K)" current=0.030 package="3 mm [THT]"]
  R2 = Resistor [tolerance=±20% power=0.25 resistance=220 mn=GND package=THT]
  J3 = female pin header, 2 pins [form="♀ (female)" mpn=A4]
  R3 = Resistor [tolerance=±20% power=0.25 resistance=220 mn=GND package=THT]
  R4 = Resistor [tolerance=±20% power=0.25 resistance=220 mn=GND package=THT]
  R5 = Resistor [tolerance=±20% power=0.25 resistance=220 mn=GND package=THT]
  R6 = Resistor [tolerance=±20% power=0.25 resistance=220 mn=GND package=THT]
  J5 = female pin header, 2 pins [form="♀ (female)" mpn=A2]
  J6 = female pin header, 2 pins [form="♀ (female)" mpn=A3]
  J7 = female pin header, 2 pins [form="♀ (female)" mpn=A5]
  J4 = female pin header, 2 pins [form="♀ (female)" mpn=A1]

nets:
  N1: LED2.cathode, Head_Light.cathode, R5.Pin_1, J6.pin1
  N2: LED2.anode, Head_Light.anode, J6.pin2
  N3: Sign_Left.cathode, LED5.cathode, R2.Pin_1, J3.pin1
  N4: Sign_Left.anode, LED5.anode, J3.pin2
  N5: Sign_Right.cathode, LED6.cathode, R6.Pin_1, J7.pin1
  N6: Sign_Right.anode, LED6.anode, J7.pin2
  N7: LED7.cathode, brake_light.anode, J4.pin2
  N8: LED7.anode, brake_light.cathode, R3.Pin_1, J4.pin1
  N9: LED9.cathode, Reverse_Light.cathode, R4.Pin_1, J5.pin1
  N10: LED9.anode, Reverse_Light.anode, J5.pin2
